// Logisim project CRC.circ as structural Verilog: 2 circuits, main circuit CRC
module CRC (
  input  [7:0] A,
  input  [3:0] B,
  output [10:0] out_3
);

  wire [2:0] n4birdivider_1_c, n4birdivider_2_c, n4birdivider_3_c, n4birdivider_4_c, n4birdivider_5_c,
       n4birdivider_7_c, tmp1;

  _4birDivider u_4birdivider_1 (.A(A[7:4]), .B(B), .C(n4birdivider_1_c));  // open: D
  _4birDivider u_4birdivider_2 (.A({tmp1, 1'b0}), .B(B), .C(n4birdivider_2_c));  // open: D
  _4birDivider u_4birdivider_3 (.A({n4birdivider_1_c, A[3]}), .B(B), .C(n4birdivider_3_c));  // open: D
  _4birDivider u_4birdivider_4 (.A({n4birdivider_2_c, 1'b0}), .B(B), .C(n4birdivider_4_c));  // open: D
  _4birDivider u_4birdivider_5 (.A({n4birdivider_3_c, A[2]}), .B(B), .C(n4birdivider_5_c));  // open: D
  _4birDivider u_4birdivider_6 (.A({n4birdivider_4_c, 1'b0}), .B(B), .C(out_3[2:0]));  // open: D
  _4birDivider u_4birdivider_7 (.A({n4birdivider_5_c, A[1]}), .B(B), .C(n4birdivider_7_c));  // open: D
  _4birDivider u_4birdivider_8 (.A({n4birdivider_7_c, A[0]}), .B(B), .C(tmp1));  // open: D

  assign out_3[10:3] = A;

  // Other names for the same wires on the sheet: S[3:0] = A[7:4]
endmodule

module _4birDivider (
  input  [3:0] A,
  input  [3:0] B,
  output [2:0] C,
  output D
);

  wire [3:0] xor_1_out;

  assign xor_1_out = A ^ B;  // XOR_Gate xor_1, 4 bits wide
  Multiplexer #(.width(3), .enable("false")) multiplexer_1 (.in0(A[2:0]), .in1(xor_1_out[2:0]), .out(C), .sel(A[3]));

  assign D = A[3];

  // Other names for the same wires on the sheet: 被除数[3:0] = A; 余数[2:0] = C; 商 = A[3]; 最高位 = A[3]; 除数[3:0] = B

  // Notes on the sheet:
  //   判断被除数最高位
endmodule
