// Logisim project bavi_moore.circ as structural Verilog: 2 circuits, main circuit navigation
module navigation (
  input  [1:0] dir,
  input  clk,
  input  reset,
  output out_4,
  output out_5
);

  wire [2:1] state;
  wire [3:0] next_state;

  Register #(.width(4)) register_1 (.D(next_state), .Q({out_4, state, out_5}), .clk(clk), .clr(reset));  // open: en
  state_transfer state_transfer_1 (
    .S3(out_4), .S2(state[2]), .S1(state[1]), .S0(out_5), .I1(dir[1]), .I0(dir[0]), .A3(next_state[3]),
    .A2(next_state[2]), .A1(next_state[1]), .A0(next_state[0]));

  // Other names for the same wires on the sheet: hit = out_5; state (some bits) = {out_4, out_5}; arrive = out_4
endmodule

module state_transfer (
  input  S3,
  input  S2,
  input  S1,
  input  S0,
  input  I1,
  input  I0,
  output A3,
  output A2,
  output A1,
  output A0
);

  wire and_1_out, and_2_out, and_3_out, and_4_out, and_5_out, and_6_out, and_7_out, and_8_out, and_9_out,
       and_10_out, and_11_out, and_12_out, and_13_out, and_14_out, and_15_out, and_16_out, not_1_out,
       not_2_out, not_3_out, not_4_out, not_5_out, not_6_out, not_7_out, not_8_out, not_9_out, not_10_out,
       not_11_out, not_12_out, not_13_out, not_14_out, not_15_out, not_16_out, not_17_out, not_18_out,
       not_19_out, not_20_out, not_21_out, not_22_out, not_23_out, not_24_out, not_25_out, not_26_out,
       not_27_out, not_28_out;

  not not_1 (not_1_out, S1);
  not not_2 (not_2_out, I1);
  not not_3 (not_3_out, I0);
  not not_4 (not_4_out, I1);
  not not_5 (not_5_out, S2);
  not not_6 (not_6_out, I1);
  not not_7 (not_7_out, I1);
  not not_8 (not_8_out, I0);
  not not_9 (not_9_out, S1);
  not not_10 (not_10_out, I1);
  not not_11 (not_11_out, S1);
  not not_12 (not_12_out, I0);
  not not_13 (not_13_out, S3);
  not not_14 (not_14_out, S2);
  not not_15 (not_15_out, I1);
  not not_16 (not_16_out, I0);
  not not_17 (not_17_out, I0);
  not not_18 (not_18_out, S3);
  not not_19 (not_19_out, S1);
  not not_20 (not_20_out, I1);
  not not_21 (not_21_out, S3);
  not not_22 (not_22_out, S2);
  not not_23 (not_23_out, S1);
  not not_24 (not_24_out, S3);
  not not_25 (not_25_out, S1);
  not not_26 (not_26_out, I0);
  not not_27 (not_27_out, I1);
  not not_28 (not_28_out, I0);
  and and_1 (and_1_out, S2, not_1_out, not_2_out, not_3_out);
  and and_2 (and_2_out, S2, S1, not_4_out, I0);
  and and_3 (and_3_out, not_5_out, S1, not_6_out);
  and and_4 (and_4_out, S1, not_7_out, not_8_out);
  and and_5 (and_5_out, S2, not_9_out, not_10_out, I0);
  and and_6 (and_6_out, S2, not_11_out, I1, not_12_out);
  and and_7 (and_7_out, S2, S1, I1, I0);
  and and_8 (and_8_out, not_13_out, not_14_out, not_15_out, not_16_out);
  and and_9 (and_9_out, S1, I1, I0);
  and and_10 (and_10_out, S2, I1, I0);
  and and_11 (and_11_out, S2, S1, not_17_out);
  and and_12 (and_12_out, not_18_out, not_19_out, not_20_out, I0);
  and and_13 (and_13_out, not_21_out, not_22_out, not_23_out, I1);
  and and_14 (and_14_out, not_24_out, not_25_out, I1, not_26_out);
  and and_15 (and_15_out, S1, I1, I0);
  and and_16 (and_16_out, S2, S1, not_27_out, not_28_out);
  or or_1 (A3, and_1_out, and_2_out);
  or or_2 (A2, and_3_out, and_4_out, and_5_out, and_6_out, and_7_out);
  or or_3 (A1, and_8_out, and_9_out, and_10_out, and_11_out);
  or or_4 (A0, and_12_out, and_13_out, and_14_out, and_15_out, and_16_out);
endmodule
