// Logisim project fsm.circ as structural Verilog: 3 circuits, main circuit fsm
module fsm (
  input  in_1,
  input  [1:0] in_2,
  output out_3
);

  wire clk, in0, in1, multiplexer_1_out, multiplexer_2_out, out0, out1;

  Clock clock_1 (.out(clk));
  Multiplexer #(.enable("false")) multiplexer_1 (.in0(in1), .in1(1'b0), .out(multiplexer_1_out), .sel(in_1));
  Multiplexer #(.enable("false")) multiplexer_2 (.in0(in0), .in1(1'b0), .out(multiplexer_2_out), .sel(in_1));
  Register #(.width(1)) register_1 (.D(multiplexer_1_out), .Q(out1), .clk(clk));  // open: en, clr
  Register #(.width(1)) register_2 (.D(multiplexer_2_out), .Q(out0), .clk(clk));  // open: en, clr
  state_transfer state_transfer_1 (.S1(out1), .S0(out0), .I1(in_2[1]), .I0(in_2[0]), .N1(in1), .N0(in0));
  \output  output_1 (.S1(out1), .S0(out0), .I1(in_2[1]), .I0(in_2[0]), .O(out_3));

  // Other names for the same wires on the sheet: input[1:0] = in_2; reset = in_1
endmodule

module state_transfer (
  input  S1,
  input  S0,
  input  I1,
  input  I0,
  output N1,
  output N0
);

  wire and_2_out, and_3_out, not_1_out, not_2_out, not_3_out, not_4_out, not_5_out, not_6_out;

  not not_1 (not_1_out, S1);
  and and_1 (N1, not_1_out, S0, not_2_out);
  not not_2 (not_2_out, I0);
  not not_3 (not_3_out, S1);
  not not_4 (not_4_out, I1);
  and and_2 (and_2_out, not_3_out, not_4_out, I0);
  not not_5 (not_5_out, S0);
  and and_3 (and_3_out, not_5_out, not_6_out, I0);
  not not_6 (not_6_out, I1);
  or or_1 (N0, and_2_out, and_3_out);
endmodule

module \output  (
  input  S1,
  input  S0,
  input  I1,
  input  I0,
  output O
);

  wire not_1_out, not_2_out;

  and and_1 (O, S1, not_1_out, not_2_out);
  not not_1 (not_1_out, S0);
  not not_2 (not_2_out, I0);
endmodule
