// Logisim project ftoi.circ as structural Verilog: 1 circuit, main circuit ftoi
module ftoi (
  input  [15:0] in_1,
  output [31:0] out_2
);

  wire comparator_1_eq, comparator_2_lt, select;
  wire [4:0] subtractor_1_out;
  wire [10:0] bit_extender_1_out;
  wire [31:0] adder_1_out, bit_extender_2_out, multiplexer_1_out, not_1_out, shifter_1_out, shifter_2_out;

  // Probe on in_1[14:10]
  // Probe on 5'b01111
  Subtractor #(.width(5)) subtractor_1 (.a(in_1[14:10]), .b(5'b01111), .out(subtractor_1_out));  // open: bin, bout
  // Probe on subtractor_1_out
  Comparator #(.width(5), .mode("unsigned")) comparator_1 (
    .a({5{1'b0}}), .b(in_1[14:10]), .eq(comparator_1_eq));  // open: gt, lt
  Comparator #(.width(5), .mode("unsigned")) comparator_2 (
    .a(in_1[14:10]), .b(5'b01111), .lt(comparator_2_lt));  // open: gt, eq
  assign bit_extender_1_out = {{1{1'b1}}, in_1[9:0]};  // Bit_Extender bit_extender_1
  // Probe on bit_extender_1_out
  or or_1 (select, comparator_1_eq, comparator_2_lt);
  assign bit_extender_2_out = {{21{1'b0}}, bit_extender_1_out};  // Bit_Extender bit_extender_2
  // Probe on shifter_1_out
  Shifter #(.width(32)) shifter_1 (.in(bit_extender_2_out), .\dist (subtractor_1_out), .out(shifter_1_out));
  Shifter #(.width(32), .shift("lr")) shifter_2 (.in(shifter_1_out), .\dist (5'b01010), .out(shifter_2_out));
  assign not_1_out = ~shifter_2_out;  // NOT_Gate not_1, 32 bits wide
  Adder #(.width(32)) adder_1 (.a(not_1_out), .b(32'h1), .out(adder_1_out));  // open: cin, cout
  Multiplexer #(.width(32), .enable("false")) multiplexer_1 (
    .in0(shifter_2_out), .in1(adder_1_out), .out(multiplexer_1_out), .sel(in_1[15]));
  Multiplexer #(.width(32), .enable("false")) multiplexer_2 (
    .in0(multiplexer_1_out), .in1({32{1'b0}}), .out(out_2), .sel(select));

  // Other names for the same wires on the sheet: float[15:0] = in_1; negative = in_1[15]
endmodule
