// Logisim project navigation.circ as structural Verilog: 4 circuits, main circuit navigation
module navigation (
  input  [1:0] dir,
  input  clk,
  input  reset,
  output out_4,
  output out_5
);

  wire hitted_1_h, in0, in1, in2, out0, out1, out2;

  Register #(.width(1)) register_1 (.D(in2), .Q(out2), .clk(clk), .clr(reset));  // open: en
  Register #(.width(1)) register_2 (.D(in1), .Q(out1), .clk(clk), .clr(reset));  // open: en
  Register #(.width(1)) register_3 (.D(in0), .Q(out0), .clk(clk), .clr(reset));  // open: en
  state_transfer state_transfer_1 (
    .S2(out2), .S1(out1), .S0(out0), .I1(dir[1]), .I0(dir[0]), .R2(in2), .R1(in1), .R0(in0));
  arrival arrival_1 (.S2(out2), .S1(out1), .S0(out0), .A(out_4));
  Register #(.width(1)) register_4 (.D(hitted_1_h), .Q(out_5), .clk(clk), .clr(reset));  // open: en
  hitted hitted_1 (.S2(out2), .S1(out1), .S0(out0), .I1(dir[1]), .I0(dir[0]), .H(hitted_1_h));

  // Other names for the same wires on the sheet: arrive = out_4; hit = out_5; input[1:0] = dir
endmodule

module state_transfer (
  input  S2,
  input  S1,
  input  S0,
  input  I1,
  input  I0,
  output R2,
  output R1,
  output R0
);

  wire and_1_out, and_2_out, and_3_out, and_4_out, and_5_out, and_6_out, and_7_out, and_8_out, and_9_out,
       and_10_out, and_11_out, not_1_out, not_2_out, not_3_out, not_4_out, not_5_out, not_6_out, not_7_out,
       not_8_out, not_9_out, not_10_out, not_11_out, not_12_out, not_13_out, not_14_out, not_15_out,
       not_16_out, not_17_out;

  not not_1 (not_1_out, S0);
  not not_2 (not_2_out, I1);
  not not_3 (not_3_out, I0);
  not not_4 (not_4_out, I1);
  not not_5 (not_5_out, S1);
  not not_6 (not_6_out, I1);
  not not_7 (not_7_out, I1);
  not not_8 (not_8_out, I0);
  not not_9 (not_9_out, S0);
  not not_10 (not_10_out, I1);
  not not_11 (not_11_out, S0);
  not not_12 (not_12_out, I0);
  not not_13 (not_13_out, S2);
  not not_14 (not_14_out, S1);
  not not_15 (not_15_out, I1);
  not not_16 (not_16_out, I0);
  not not_17 (not_17_out, I0);
  and and_1 (and_1_out, S1, not_1_out, not_2_out, not_3_out);
  and and_2 (and_2_out, S1, S0, not_4_out, I0);
  and and_3 (and_3_out, not_5_out, S0, not_6_out);
  and and_4 (and_4_out, S0, not_7_out, not_8_out);
  and and_5 (and_5_out, S1, not_9_out, not_10_out, I0);
  and and_6 (and_6_out, S1, not_11_out, I1, not_12_out);
  and and_7 (and_7_out, S1, S0, I1, I0);
  and and_8 (and_8_out, not_13_out, not_14_out, not_15_out, not_16_out);
  and and_9 (and_9_out, S0, I1, I0);
  and and_10 (and_10_out, S1, I1, I0);
  and and_11 (and_11_out, S1, S0, not_17_out);
  or or_1 (R2, and_1_out, and_2_out);
  or or_2 (R1, and_3_out, and_4_out, and_5_out, and_6_out, and_7_out);
  or or_3 (R0, and_8_out, and_9_out, and_10_out, and_11_out);
endmodule

module arrival (
  input  S2,
  input  S1,
  input  S0,
  output A
);


  assign A = S2;
endmodule

module hitted (
  input  S2,
  input  S1,
  input  S0,
  input  I1,
  input  I0,
  output H
);

  wire and_1_out, and_2_out, and_3_out, and_4_out, and_5_out, not_1_out, not_2_out, not_3_out, not_4_out,
       not_5_out, not_6_out, not_7_out, not_8_out, not_9_out, not_10_out, not_11_out, not_12_out, not_13_out;

  not not_1 (not_1_out, S2);
  not not_2 (not_2_out, S0);
  not not_3 (not_3_out, I1);
  not not_4 (not_4_out, S2);
  not not_5 (not_5_out, S1);
  not not_6 (not_6_out, S0);
  not not_7 (not_7_out, S2);
  not not_8 (not_8_out, S0);
  not not_9 (not_9_out, I0);
  not not_10 (not_10_out, S2);
  not not_11 (not_11_out, S2);
  not not_12 (not_12_out, I1);
  not not_13 (not_13_out, I0);
  and and_1 (and_1_out, not_1_out, not_2_out, not_3_out, I0);
  and and_2 (and_2_out, not_4_out, not_5_out, not_6_out, I1);
  and and_3 (and_3_out, not_7_out, not_8_out, I1, not_9_out);
  and and_4 (and_4_out, not_10_out, S0, I1, I0);
  and and_5 (and_5_out, not_11_out, S1, S0, not_12_out, not_13_out);
  or or_1 (H, and_1_out, and_2_out, and_3_out, and_4_out, and_5_out);
endmodule
