// Logisim project CPUvP3 - 提交版本v0.circ as structural Verilog: 7 circuits, main circuit main
module main (
  input  in_1,
  output [31:0] out_2,
  output [31:0] out_3,
  output out_4,
  output [4:0] out_5,
  output [31:0] out_6,
  output out_7,
  output [31:0] out_8,
  output [31:0] out_9
);

  wire alu_1_zero, ALUSrc, beq, branch, clock_1_out, ExtOp, MemToReg, RegDst;
  wire [2:0] controller_1_aluop;
  wire [31:0] dm_1_rd, ext_1_result, grf_1_rd1, multiplexer_2_out;

  Clock clock_1 (.out(clock_1_out));
  IFU ifu_1 (.clk(clock_1_out), .reset(in_1), .Instr(out_2), .off(ext_1_result), .branch(branch), .out_6(out_3));
  // Probe on out_2[31:26]
  // Probe on out_2[5:0]
  // Probe on controller_1_aluop
  EXT ext_1 (.num(out_2[15:0]), .sel(ExtOp), .result(ext_1_result));
  Controller controller_1 (
    .op(out_2[31:26]), .funct(out_2[5:0]), .ALUop(controller_1_aluop), .RegWrite(out_4), .RegDst(RegDst),
    .beq(beq), .MemWrite(out_7), .MemToReg(MemToReg), .ExtOp(ExtOp), .ALUSrc(ALUSrc));
  Multiplexer #(.width(5), .enable("false")) multiplexer_1 (
    .in0(out_2[20:16]), .in1(out_2[15:11]), .out(out_5), .sel(RegDst));
  GRF grf_1 (
    .clk(clock_1_out), .A1(out_2[25:21]), .reset(in_1), .A2(out_2[20:16]), .WD(out_6), .WE(out_4),
    .A3(out_5), .RD1(grf_1_rd1), .RD2(out_9));
  Multiplexer #(.width(32), .enable("false")) multiplexer_2 (
    .in0(out_9), .in1(ext_1_result), .out(multiplexer_2_out), .sel(ALUSrc));
  ALU alu_1 (.A(grf_1_rd1), .B(multiplexer_2_out), .aluop(controller_1_aluop), .res(out_8), .zero(alu_1_zero));
  and and_1 (branch, beq, alu_1_zero);
  DM dm_1 (.A(out_8), .WE(out_7), .clk(clock_1_out), .reset(in_1), .WD(out_9), .RD(dm_1_rd));
  Multiplexer #(.width(32), .enable("false")) multiplexer_3 (.in0(out_8), .in1(dm_1_rd), .out(out_6), .sel(MemToReg));

  // Other names for the same wires on the sheet: A3[4:0] = out_5; Instr[31:0] = out_2; MemAddr[31:0] = out_8;
  //   MemData[31:0] = out_9; MemWrite = out_7; PC[31:0] = out_3; RegWrite = out_4; WD[31:0] = out_6
endmodule

module GRF (
  input  clk,
  input  [4:0] A1,
  input  reset,
  input  [4:0] A2,
  input  [31:0] WD,
  input  WE,
  input  [4:0] A3,
  output [31:0] RD1,
  output [31:0] RD2
);

  wire [31:0] in1, in2, in3, in4, in5, in6, in7, in8, in9, in10, in11, in12, in13, in14, in15, in16, in17,
       in18, in19, in20, in21, in22, in23, in24, in25, in26, in27, in28, in29, in30, in31, out0, out1, out2,
       out3, out4, out5, out6, out7, out8, out9, out10, out11, out12, out13, out14, out15, out16, out17,
       out18, out19, out20, out21, out22, out23, out24, out25, out26, out27, out28, out29, out30, out31;

  Register #(.width(32)) register_1 (.D({32{1'b0}}), .en(WE), .Q(out0), .clk(clk), .clr(reset));
  Register #(.width(32)) register_2 (.D(in8), .en(WE), .Q(out8), .clk(clk), .clr(reset));
  Register #(.width(32)) register_3 (.D(in16), .en(WE), .Q(out16), .clk(clk), .clr(reset));
  Register #(.width(32)) register_4 (.D(in24), .en(WE), .Q(out24), .clk(clk), .clr(reset));
  Register #(.width(32)) register_5 (.D(in1), .en(WE), .Q(out1), .clk(clk), .clr(reset));
  Register #(.width(32)) register_6 (.D(in9), .en(WE), .Q(out9), .clk(clk), .clr(reset));
  Register #(.width(32)) register_7 (.D(in17), .en(WE), .Q(out17), .clk(clk), .clr(reset));
  Register #(.width(32)) register_8 (.D(in25), .en(WE), .Q(out25), .clk(clk), .clr(reset));
  Multiplexer #(.select(5), .width(32), .enable("false")) multiplexer_1 (
    .in0(out0), .in1(out1), .in2(out2), .in3(out3), .in4(out4), .in5(out5), .in6(out6), .in7(out7),
    .in8(out8), .in9(out9), .in10(out10), .in11(out11), .in12(out12), .in13(out13), .in14(out14),
    .in15(out15), .in16(out16), .in17(out17), .in18(out18), .in19(out19), .in20(out20), .in21(out21),
    .in22(out22), .in23(out23), .in24(out24), .in25(out25), .in26(out26), .in27(out27), .in28(out28),
    .in29(out29), .in30(out30), .in31(out31), .out(RD1), .sel(A1));
  Register #(.width(32)) register_9 (.D(in2), .en(WE), .Q(out2), .clk(clk), .clr(reset));
  Register #(.width(32)) register_10 (.D(in10), .en(WE), .Q(out10), .clk(clk), .clr(reset));
  Register #(.width(32)) register_11 (.D(in18), .en(WE), .Q(out18), .clk(clk), .clr(reset));
  Register #(.width(32)) register_12 (.D(in26), .en(WE), .Q(out26), .clk(clk), .clr(reset));
  Register #(.width(32)) register_13 (.D(in3), .en(WE), .Q(out3), .clk(clk), .clr(reset));
  Register #(.width(32)) register_14 (.D(in11), .en(WE), .Q(out11), .clk(clk), .clr(reset));
  Register #(.width(32)) register_15 (.D(in19), .en(WE), .Q(out19), .clk(clk), .clr(reset));
  Register #(.width(32)) register_16 (.D(in27), .en(WE), .Q(out27), .clk(clk), .clr(reset));
  Multiplexer #(.select(5), .width(32), .enable("false")) multiplexer_2 (
    .in0(out0), .in1(out1), .in2(out2), .in3(out3), .in4(out4), .in5(out5), .in6(out6), .in7(out7),
    .in8(out8), .in9(out9), .in10(out10), .in11(out11), .in12(out12), .in13(out13), .in14(out14),
    .in15(out15), .in16(out16), .in17(out17), .in18(out18), .in19(out19), .in20(out20), .in21(out21),
    .in22(out22), .in23(out23), .in24(out24), .in25(out25), .in26(out26), .in27(out27), .in28(out28),
    .in29(out29), .in30(out30), .in31(out31), .out(RD2), .sel(A2));
  Demultiplexer #(.select(5), .width(32), .tristate("true"), .enable("false")) demultiplexer_1 (
    .out1(in1), .out2(in2), .out3(in3), .out4(in4), .out5(in5), .out6(in6), .out7(in7), .out8(in8),
    .out9(in9), .out10(in10), .out11(in11), .out12(in12), .out13(in13), .out14(in14), .out15(in15),
    .out16(in16), .out17(in17), .out18(in18), .out19(in19), .out20(in20), .out21(in21), .out22(in22),
    .out23(in23), .out24(in24), .out25(in25), .out26(in26), .out27(in27), .out28(in28), .out29(in29),
    .out30(in30), .out31(in31), .in(WD), .sel(A3));  // open: out0
  Register #(.width(32)) register_17 (.D(in4), .en(WE), .Q(out4), .clk(clk), .clr(reset));
  Register #(.width(32)) register_18 (.D(in12), .en(WE), .Q(out12), .clk(clk), .clr(reset));
  Register #(.width(32)) register_19 (.D(in20), .en(WE), .Q(out20), .clk(clk), .clr(reset));
  Register #(.width(32)) register_20 (.D(in28), .en(WE), .Q(out28), .clk(clk), .clr(reset));
  Register #(.width(32)) register_21 (.D(in5), .en(WE), .Q(out5), .clk(clk), .clr(reset));
  Register #(.width(32)) register_22 (.D(in13), .en(WE), .Q(out13), .clk(clk), .clr(reset));
  Register #(.width(32)) register_23 (.D(in21), .en(WE), .Q(out21), .clk(clk), .clr(reset));
  Register #(.width(32)) register_24 (.D(in29), .en(WE), .Q(out29), .clk(clk), .clr(reset));
  Register #(.width(32)) register_25 (.D(in6), .en(WE), .Q(out6), .clk(clk), .clr(reset));
  Register #(.width(32)) register_26 (.D(in14), .en(WE), .Q(out14), .clk(clk), .clr(reset));
  Register #(.width(32)) register_27 (.D(in22), .en(WE), .Q(out22), .clk(clk), .clr(reset));
  Register #(.width(32)) register_28 (.D(in30), .en(WE), .Q(out30), .clk(clk), .clr(reset));
  Register #(.width(32)) register_29 (.D(in7), .en(WE), .Q(out7), .clk(clk), .clr(reset));
  Register #(.width(32)) register_30 (.D(in15), .en(WE), .Q(out15), .clk(clk), .clr(reset));
  Register #(.width(32)) register_31 (.D(in23), .en(WE), .Q(out23), .clk(clk), .clr(reset));
  Register #(.width(32)) register_32 (.D(in31), .en(WE), .Q(out31), .clk(clk), .clr(reset));
endmodule

module IFU (
  input  clk,
  input  reset,
  input  [31:0] off,
  input  branch,
  output [31:0] Instr,
  output [31:0] out_6
);

  wire [31:0] adder_1_out, adder_2_out, next, register_1_q, shifter_1_out;

  // Probe on next
  // Probe on register_1_q[13:2]
  Register #(.width(32)) register_1 (.D(next), .en(1'b1), .Q(register_1_q), .clk(clk), .clr(reset));
  Adder #(.width(32)) adder_1 (.a(register_1_q), .b(32'h4), .out(adder_1_out));  // open: cin, cout
  Shifter #(.width(32)) shifter_1 (.in(off), .\dist (5'b00010), .out(shifter_1_out));
  // Probe on shifter_1_out
  // Probe on adder_1_out
  ROM #(.addrWidth(12), .dataWidth(32)) rom_1 (.addr(register_1_q[13:2]), .data(Instr));  // open: sel
  Adder #(.width(32)) adder_2 (.a(shifter_1_out), .b(adder_1_out), .out(adder_2_out));  // open: cin, cout
  Adder #(.width(32)) adder_3 (.a(register_1_q), .b(32'h3000), .out(out_6));  // open: cin, cout
  Multiplexer #(.width(32), .enable("false")) multiplexer_1 (
    .in0(adder_1_out), .in1(adder_2_out), .out(next), .sel(branch));
  // Probe on adder_2_out

  // Notes on the sheet:
  //   IM
  //   contents of rom_1 (hex, n*v repeats v):
  //   3408009c 340a0087 34e7040b 3c050065 340508a3 0 116a0008 358c0008 3c1600aa 16c5820 1405820 8d300004
  //   1495020 1405822 116afff7 3c022b67
endmodule

module ALU (
  input  [31:0] A,
  input  [31:0] B,
  input  [2:0] aluop,
  output zero,
  output [31:0] res
);

  wire comparator_2_lt, comparator_3_lt;
  wire [31:0] a_b, a_b_t, adder_2_out, alui16, aorb, multiplexer_1_out, multiplexer_3_out;

  Comparator #(.width(32)) comparator_1 (.a(A), .b(B), .eq(zero));  // open: gt, lt
  Adder #(.width(32)) adder_1 (.a(A), .b(B), .out(a_b));  // open: cin, cout
  Subtractor #(.width(32)) subtractor_1 (.a(A), .b(B), .out(a_b_t));  // open: bin, bout
  assign aorb = A | B;  // OR_Gate or_1, 32 bits wide
  Shifter #(.width(32)) shifter_1 (.in(B), .\dist (5'b10000), .out(alui16));
  Adder #(.width(32)) adder_2 (.a(B), .b(A), .out(adder_2_out));  // open: cin, cout
  // Probe on adder_2_out
  // Probe on B
  Comparator #(.width(32)) comparator_2 (.a(adder_2_out), .b(B), .lt(comparator_2_lt));  // open: gt, eq
  Multiplexer #(.width(32), .enable("false")) multiplexer_1 (
    .in0(adder_2_out), .in1(B), .out(multiplexer_1_out), .sel(comparator_2_lt));
  // Probe on multiplexer_1_out
  // Probe on A
  Multiplexer #(.select(3), .width(32), .enable("false")) multiplexer_2 (
    .in0(a_b), .in1(a_b_t), .in2(aorb), .in3(alui16), .in4(multiplexer_3_out), .out(res), .sel(aluop));  // open: in5, in6, in7
  Comparator #(.width(32)) comparator_3 (.a(multiplexer_1_out), .b(A), .lt(comparator_3_lt));  // open: gt, eq
  // Probe on multiplexer_3_out
  Multiplexer #(.width(32), .enable("false")) multiplexer_3 (
    .in0(multiplexer_1_out), .in1(A), .out(multiplexer_3_out), .sel(comparator_3_lt));
endmodule

module EXT (
  input  [15:0] num,
  input  sel,
  output [31:0] result
);

  wire [31:0] bit_extender_1_out, bit_extender_2_out;

  assign bit_extender_1_out = {{16{1'b0}}, num};  // Bit_Extender bit_extender_1
  assign bit_extender_2_out = {{16{num[15]}}, num};  // Bit_Extender bit_extender_2
  Multiplexer #(.width(32), .enable("false")) multiplexer_1 (
    .in0(bit_extender_1_out), .in1(bit_extender_2_out), .out(result), .sel(sel));
endmodule

module DM (
  input  [31:0] A,
  input  WE,
  input  clk,
  input  reset,
  input  [31:0] WD,
  output [31:0] RD
);

  RAM #(.addrWidth(12), .dataWidth(32), .bus("separate")) ram_1 (
    .addr(A[13:2]), .din(WD), .data(RD), .str(WE), .clk(clk), .clr(reset));  // open: sel, ld
endmodule

module Controller (
  input  [5:0] op,
  input  [5:0] funct,
  output RegWrite,
  output RegDst,
  output beq,
  output MemWrite,
  output MemToReg,
  output ExtOp,
  output ALUSrc,
  output [2:0] ALUop
);

  wire add, addm, beq_t, bitfinder_1_found, comparator_1_eq, lui, lw, ori, sub, sw;
  wire [2:0] bitfinder_1_index;
  wire [3:0] or_6_out;

  Comparator #(.width(6), .mode("unsigned")) comparator_1 (
    .a(op), .b({6{1'b0}}), .eq(comparator_1_eq));  // open: gt, lt
  and u_add (add, comparator_1_eq, funct[5], ~funct[4], ~funct[3], ~funct[2], ~funct[1], ~funct[0]);  // AND_Gate
  and u_sub (sub, comparator_1_eq, funct[5], ~funct[4], ~funct[3], ~funct[2], funct[1], ~funct[0]);  // AND_Gate
  and u_ori (ori, ~comparator_1_eq, ~op[5], ~op[4], op[3], op[2], ~op[1], op[0]);  // AND_Gate
  and u_lw (lw, ~comparator_1_eq, op[5], ~op[4], ~op[3], ~op[2], op[1], op[0]);  // AND_Gate
  and u_sw (sw, ~comparator_1_eq, op[5], ~op[4], op[3], ~op[2], op[1], op[0]);  // AND_Gate
  and u_beq (beq_t, ~comparator_1_eq, ~op[5], ~op[4], ~op[3], op[2], ~op[1], ~op[0]);  // AND_Gate
  and u_lui (lui, ~comparator_1_eq, ~op[5], ~op[4], op[3], op[2], op[1], op[0]);  // AND_Gate
  and u_addm (addm, comparator_1_eq, ~funct[5], ~funct[4], funct[3], funct[2], funct[1], ~funct[0]);  // AND_Gate
  or or_1 (RegWrite, add, sub, ori, lw, addm, lui);
  or or_2 (or_6_out[1], sub, beq_t);
  buf or_3 (or_6_out[2], ori);  // OR_Gate
  buf or_4 (or_6_out[3], lui);  // OR_Gate
  or or_5 (RegDst, add, sub, addm);
  or or_6 (or_6_out[0], lw, add, sw);
  buf or_7 (beq, beq_t);  // OR_Gate
  buf or_8 (MemWrite, sw);  // OR_Gate
  BitFinder #(.width(5)) bitfinder_1 (.in({addm, or_6_out}), .index(bitfinder_1_index), .found(bitfinder_1_found));
  Multiplexer #(.width(3), .enable("false")) multiplexer_1 (
    .in0(3'b000), .in1(bitfinder_1_index), .out(ALUop), .sel(bitfinder_1_found));
  buf or_9 (MemToReg, lw);  // OR_Gate
  or or_10 (ExtOp, ~ori, lw, sw);  // OR_Gate
  or or_11 (ALUSrc, ori, lw, sw, lui);
endmodule
