// Logisim project CPUvP3 - 提交版本v1 - 副本.circ as structural Verilog: 7 circuits, main circuit main
module main (
  input  in_1,
  output [31:0] out_2,
  output [31:0] out_3,
  output out_4,
  output [4:0] out_5,
  output [31:0] out_6,
  output out_7,
  output [31:0] out_8,
  output [31:0] out_9
);

  wire alu_1_out_6, ALUSrc, clock_1_out, Extop;
  wire [1:0] alu_1_comp, DMop, MemToReg, PCsel, RegDst;
  wire [2:0] controller_1_aluop;
  wire [31:0] dm_1_rd, ext_1_result, ifu_1_pc_4, multiplexer_3_out, ra;

  // Probe on out_3
  Clock clock_1 (.out(clock_1_out));
  // Probe on out_2
  IFU ifu_1 (
    .Instr(out_2), .clk(clock_1_out), .reset(in_1), .PC_4(ifu_1_pc_4), .PC(out_3), .offset(out_2[15:0]),
    .Register(ra), .imm(out_2[25:0]), .PCsel(PCsel));
  Multiplexer #(.select(2), .width(32), .enable("false")) multiplexer_1 (
    .in0(out_8), .in1(dm_1_rd), .in2(ifu_1_pc_4), .out(out_6), .sel(MemToReg));  // open: in3
  Controller controller_1 (
    .op(out_2[31:26]), .funct(out_2[5:0]), .ALUop(controller_1_aluop), .RegDst(RegDst), .ALUSrc(ALUSrc),
    .MemToReg(MemToReg), .RegWrite(out_4), .MemWrite(out_7), .PCsel(PCsel), .DMop(DMop), .comp(alu_1_comp),
    .Extop(Extop), .in_4(alu_1_out_6));
  Multiplexer #(.select(2), .width(5), .enable("false")) multiplexer_2 (
    .in0(out_2[20:16]), .in1(out_2[15:11]), .in2({5{1'b1}}), .out(out_5), .sel(RegDst));  // open: in3
  EXT ext_1 (.num(out_2[15:0]), .sel(Extop), .result(ext_1_result));
  // Probe on controller_1_aluop
  // Probe on RegDst
  // Probe on DMop
  // Probe on alu_1_comp
  GRF grf_1 (
    .clk(clock_1_out), .A1(out_2[25:21]), .reset(in_1), .A2(out_2[20:16]), .WD(out_6), .WE(out_4),
    .A3(out_5), .RD1(ra), .RD2(out_9));
  // Probe on MemToReg
  // Probe on PCsel
  Multiplexer #(.width(32), .enable("false")) multiplexer_3 (
    .in0(out_9), .in1(ext_1_result), .out(multiplexer_3_out), .sel(ALUSrc));
  ALU alu_1 (
    .A(ra), .B(multiplexer_3_out), .comp(alu_1_comp), .ALUop(controller_1_aluop), .result(out_8),
    .out_6(alu_1_out_6));
  DM dm_1 (.A(out_8), .WE(out_7), .clk(clock_1_out), .reset(in_1), .WD(out_9), .RD(dm_1_rd), .DMop(DMop));

  // Other names for the same wires on the sheet: A3[4:0] = out_5; Instr[31:0] = out_2; offset[15:0] = out_2[15:0];
  //   MemAddr[31:0] = out_8; MemData[31:0] = out_9; MemWrite = out_7; PC[31:0] = out_3; RegWrite = out_4;
  //   WD[31:0] = out_6
endmodule

module GRF (
  input  clk,
  input  [4:0] A1,
  input  reset,
  input  [4:0] A2,
  input  [31:0] WD,
  input  WE,
  input  [4:0] A3,
  output [31:0] RD1,
  output [31:0] RD2
);

  wire [31:0] in1, in2, in3, in4, in5, in6, in7, in8, in9, in10, in11, in12, in13, in14, in15, in16, in17,
       in18, in19, in20, in21, in22, in23, in24, in25, in26, in27, in28, in29, in30, in31, out0, out1, out2,
       out3, out4, out5, out6, out7, out8, out9, out10, out11, out12, out13, out14, out15, out16, out17,
       out18, out19, out20, out21, out22, out23, out24, out25, out26, out27, out28, out29, out30, out31;

  Register #(.width(32)) register_1 (.D({32{1'b0}}), .en(WE), .Q(out0), .clk(clk), .clr(reset));
  Register #(.width(32)) register_2 (.D(in8), .en(WE), .Q(out8), .clk(clk), .clr(reset));
  Register #(.width(32)) register_3 (.D(in16), .en(WE), .Q(out16), .clk(clk), .clr(reset));
  Register #(.width(32)) register_4 (.D(in24), .en(WE), .Q(out24), .clk(clk), .clr(reset));
  Register #(.width(32)) register_5 (.D(in1), .en(WE), .Q(out1), .clk(clk), .clr(reset));
  Register #(.width(32)) register_6 (.D(in9), .en(WE), .Q(out9), .clk(clk), .clr(reset));
  Register #(.width(32)) register_7 (.D(in17), .en(WE), .Q(out17), .clk(clk), .clr(reset));
  Register #(.width(32)) register_8 (.D(in25), .en(WE), .Q(out25), .clk(clk), .clr(reset));
  Multiplexer #(.select(5), .width(32), .enable("false")) multiplexer_1 (
    .in0(out0), .in1(out1), .in2(out2), .in3(out3), .in4(out4), .in5(out5), .in6(out6), .in7(out7),
    .in8(out8), .in9(out9), .in10(out10), .in11(out11), .in12(out12), .in13(out13), .in14(out14),
    .in15(out15), .in16(out16), .in17(out17), .in18(out18), .in19(out19), .in20(out20), .in21(out21),
    .in22(out22), .in23(out23), .in24(out24), .in25(out25), .in26(out26), .in27(out27), .in28(out28),
    .in29(out29), .in30(out30), .in31(out31), .out(RD1), .sel(A1));
  Register #(.width(32)) register_9 (.D(in2), .en(WE), .Q(out2), .clk(clk), .clr(reset));
  Register #(.width(32)) register_10 (.D(in10), .en(WE), .Q(out10), .clk(clk), .clr(reset));
  Register #(.width(32)) register_11 (.D(in18), .en(WE), .Q(out18), .clk(clk), .clr(reset));
  Register #(.width(32)) register_12 (.D(in26), .en(WE), .Q(out26), .clk(clk), .clr(reset));
  Register #(.width(32)) register_13 (.D(in3), .en(WE), .Q(out3), .clk(clk), .clr(reset));
  Register #(.width(32)) register_14 (.D(in11), .en(WE), .Q(out11), .clk(clk), .clr(reset));
  Register #(.width(32)) register_15 (.D(in19), .en(WE), .Q(out19), .clk(clk), .clr(reset));
  Register #(.width(32)) register_16 (.D(in27), .en(WE), .Q(out27), .clk(clk), .clr(reset));
  Multiplexer #(.select(5), .width(32), .enable("false")) multiplexer_2 (
    .in0(out0), .in1(out1), .in2(out2), .in3(out3), .in4(out4), .in5(out5), .in6(out6), .in7(out7),
    .in8(out8), .in9(out9), .in10(out10), .in11(out11), .in12(out12), .in13(out13), .in14(out14),
    .in15(out15), .in16(out16), .in17(out17), .in18(out18), .in19(out19), .in20(out20), .in21(out21),
    .in22(out22), .in23(out23), .in24(out24), .in25(out25), .in26(out26), .in27(out27), .in28(out28),
    .in29(out29), .in30(out30), .in31(out31), .out(RD2), .sel(A2));
  Demultiplexer #(.select(5), .width(32), .tristate("true"), .enable("false")) demultiplexer_1 (
    .out1(in1), .out2(in2), .out3(in3), .out4(in4), .out5(in5), .out6(in6), .out7(in7), .out8(in8),
    .out9(in9), .out10(in10), .out11(in11), .out12(in12), .out13(in13), .out14(in14), .out15(in15),
    .out16(in16), .out17(in17), .out18(in18), .out19(in19), .out20(in20), .out21(in21), .out22(in22),
    .out23(in23), .out24(in24), .out25(in25), .out26(in26), .out27(in27), .out28(in28), .out29(in29),
    .out30(in30), .out31(in31), .in(WD), .sel(A3));  // open: out0
  Register #(.width(32)) register_17 (.D(in4), .en(WE), .Q(out4), .clk(clk), .clr(reset));
  Register #(.width(32)) register_18 (.D(in12), .en(WE), .Q(out12), .clk(clk), .clr(reset));
  Register #(.width(32)) register_19 (.D(in20), .en(WE), .Q(out20), .clk(clk), .clr(reset));
  Register #(.width(32)) register_20 (.D(in28), .en(WE), .Q(out28), .clk(clk), .clr(reset));
  Register #(.width(32)) register_21 (.D(in5), .en(WE), .Q(out5), .clk(clk), .clr(reset));
  Register #(.width(32)) register_22 (.D(in13), .en(WE), .Q(out13), .clk(clk), .clr(reset));
  Register #(.width(32)) register_23 (.D(in21), .en(WE), .Q(out21), .clk(clk), .clr(reset));
  Register #(.width(32)) register_24 (.D(in29), .en(WE), .Q(out29), .clk(clk), .clr(reset));
  Register #(.width(32)) register_25 (.D(in6), .en(WE), .Q(out6), .clk(clk), .clr(reset));
  Register #(.width(32)) register_26 (.D(in14), .en(WE), .Q(out14), .clk(clk), .clr(reset));
  Register #(.width(32)) register_27 (.D(in22), .en(WE), .Q(out22), .clk(clk), .clr(reset));
  Register #(.width(32)) register_28 (.D(in30), .en(WE), .Q(out30), .clk(clk), .clr(reset));
  Register #(.width(32)) register_29 (.D(in7), .en(WE), .Q(out7), .clk(clk), .clr(reset));
  Register #(.width(32)) register_30 (.D(in15), .en(WE), .Q(out15), .clk(clk), .clr(reset));
  Register #(.width(32)) register_31 (.D(in23), .en(WE), .Q(out23), .clk(clk), .clr(reset));
  Register #(.width(32)) register_32 (.D(in31), .en(WE), .Q(out31), .clk(clk), .clr(reset));
endmodule

module IFU (
  input  clk,
  input  reset,
  input  [15:0] offset,
  input  [1:0] PCsel,
  input  [25:0] imm,
  input  [31:0] Register,
  output [31:0] PC,
  output [31:0] PC_4,
  output [31:0] Instr
);

  wire [17:0] bit_extender_1_out, shifter_1_out;
  wire [31:0] adder_1_out, bit_extender_2_out, branch_PC, j_PC, jr_PC, nextPC, PC_4_t, PC_t;

  // Probe on nextPC
  assign bit_extender_1_out = {{2{1'b0}}, offset};  // Bit_Extender bit_extender_1
  Adder #(.width(32)) adder_1 (.a(PC_4_t), .b(32'h3000), .out(adder_1_out));  // open: cin, cout
  Register #(.width(32)) register_1 (.D(nextPC), .Q(PC_t), .clk(clk), .clr(reset));  // open: en
  Adder #(.width(32)) adder_2 (.a(PC_t), .b(32'h4), .out(PC_4_t));  // open: cin, cout
  assign bit_extender_2_out = {{14{shifter_1_out[17]}}, shifter_1_out};  // Bit_Extender bit_extender_2
  Shifter #(.width(18)) shifter_1 (.in(bit_extender_1_out), .\dist (5'b00010), .out(shifter_1_out));
  Subtractor #(.width(32)) subtractor_1 (.a(Register), .b(32'h3000), .out(jr_PC));  // open: bin, bout
  Adder #(.width(32)) adder_3 (.a(PC_4_t), .b(bit_extender_2_out), .out(branch_PC));  // open: cin, cout
  Subtractor #(.width(32)) subtractor_2 (
    .a({adder_1_out[31:28], imm, 2'b00}), .b(32'h3000), .out(j_PC));  // open: bin, bout
  // Probe on PC
  Adder #(.width(32)) adder_4 (.a(PC_t), .b(32'h3000), .out(PC));  // open: cin, cout
  ROM #(.addrWidth(12), .dataWidth(32)) rom_1 (.addr(PC_t[13:2]), .data(Instr));  // open: sel
  Multiplexer #(.select(2), .width(32), .enable("false")) multiplexer_1 (
    .in0(PC_4_t), .in1(branch_PC), .in2(j_PC), .in3(jr_PC), .out(nextPC), .sel(PCsel));
  Adder #(.width(32)) adder_5 (.a(PC_4_t), .b(32'h3000), .out(PC_4));  // open: cin, cout

  // Notes on the sheet:
  //   contents of rom_1 (hex, n*v repeats v):
  //   3c10f123 36103f21 3c114567 36317465 3c1289ab 3652b89a 3c13cdef 3673cfed 34080004 ac100000 ad110000
  //   ad120004 1084020 8d190000 8d18fffc 34080014 ad13fff8 34080013 a511ffff a5120001 34080019 a113ffff
  //   a1110000 a1120001 a1100002 34080002 8109fffe 810bffff 81090000 810a0001 34080013 850affff 850d0001
endmodule

module ALU (
  input  [31:0] A,
  input  [31:0] B,
  input  [2:0] ALUop,
  output [1:0] comp,
  output [31:0] result,
  output out_6
);

  wire comparator_2_eq, comparator_3_eq, comparator_4_eq, not_1_out, not_2_out;
  wire [2:0] comparator_1_gt;
  wire [5:0] bitadder_1_out, bitadder_2_out, divider_1_rem;
  wire [31:0] a_b, a_b_t, aorb, blui16;

  // Probe on bitadder_1_out
  Comparator #(.width(32)) comparator_1 (
    .a(A), .b(B), .gt(comparator_1_gt[0]), .eq(comparator_1_gt[1]), .lt(comparator_1_gt[2]));
  Adder #(.width(32)) adder_1 (.a(A), .b(B), .out(a_b));  // open: cin, cout
  Subtractor #(.width(32)) subtractor_1 (.a(A), .b(B), .out(a_b_t));  // open: bin, bout
  assign aorb = A | B;  // OR_Gate or_1, 32 bits wide
  Shifter #(.width(32)) shifter_1 (.in(B), .\dist (5'b10000), .out(blui16));
  BitAdder #(.width(32)) bitadder_1 (.in0(A), .out(bitadder_1_out));
  BitAdder #(.width(32)) bitadder_2 (.in0(B), .out(bitadder_2_out));
  BitFinder #(.width(3)) bitfinder_1 (.in(comparator_1_gt), .index(comp));  // open: found
  not not_1 (not_1_out, comparator_2_eq);
  Comparator #(.width(6)) comparator_2 (.a(bitadder_1_out), .b({6{1'b0}}), .eq(comparator_2_eq));  // open: gt, lt
  Comparator #(.width(6)) comparator_3 (.a(bitadder_2_out), .b({6{1'b0}}), .eq(comparator_3_eq));  // open: gt, lt
  not not_2 (not_2_out, comparator_3_eq);
  Divider #(.width(6)) divider_1 (.a(bitadder_1_out), .b(bitadder_2_out), .rem(divider_1_rem));  // open: out, upper
  Comparator #(.width(6)) comparator_4 (.a(divider_1_rem), .b({6{1'b0}}), .eq(comparator_4_eq));  // open: gt, lt
  and and_1 (out_6, not_1_out, not_2_out, comparator_4_eq);
  Multiplexer #(.select(3), .width(32), .enable("false")) multiplexer_1 (
    .in0(a_b), .in1(a_b_t), .in2(aorb), .in3(blui16), .out(result), .sel(ALUop));  // open: in4, in5, in6, in7
endmodule

module EXT (
  input  [15:0] num,
  input  sel,
  output [31:0] result
);

  wire [31:0] bit_extender_1_out, bit_extender_2_out;

  assign bit_extender_1_out = {{16{1'b0}}, num};  // Bit_Extender bit_extender_1
  assign bit_extender_2_out = {{16{num[15]}}, num};  // Bit_Extender bit_extender_2
  Multiplexer #(.width(32), .enable("false")) multiplexer_1 (
    .in0(bit_extender_1_out), .in1(bit_extender_2_out), .out(result), .sel(sel));
endmodule

module DM (
  input  [31:0] A,
  input  WE,
  input  clk,
  input  reset,
  input  [31:0] WD,
  input  [1:0] DMop,
  output [31:0] RD
);

  wire [7:0] multiplexer_4_out, RD7_0, RD15_8, RD23_16, RD31_24;
  wire [15:0] multiplexer_5_out;
  wire [31:0] bit_extender_1_out, bit_extender_2_out, DataIn, multiplexer_1_out, multiplexer_2_out;

  // Probe on A
  Multiplexer #(.width(32), .enable("false")) multiplexer_1 (
    .in0({RD31_24, RD23_16, WD[15:0]}), .in1({WD[15:0], RD15_8, RD7_0}), .out(multiplexer_1_out), .sel(A[1]));
  Multiplexer #(.select(2), .width(32), .enable("false")) multiplexer_2 (
    .in0({RD31_24, RD23_16, RD15_8, WD[7:0]}), .in1({RD31_24, RD23_16, WD[7:0], RD7_0}),
    .in2({RD31_24, WD[7:0], RD15_8, RD7_0}), .in3({WD[7:0], RD23_16, RD15_8, RD7_0}),
    .out(multiplexer_2_out), .sel(A[1:0]));
  RAM #(.addrWidth(12), .dataWidth(32), .bus("separate")) ram_1 (
    .addr(A[13:2]), .din(DataIn), .data({RD31_24, RD23_16, RD15_8, RD7_0}), .str(WE), .clk(clk), .clr(reset));  // open: sel, ld
  Multiplexer #(.select(2), .width(32), .enable("false")) multiplexer_3 (
    .in0(WD), .in1(multiplexer_1_out), .in2(multiplexer_2_out), .out(DataIn), .sel(DMop));  // open: in3
  Multiplexer #(.select(2), .width(8), .enable("false")) multiplexer_4 (
    .in0(RD7_0), .in1(RD15_8), .in2(RD23_16), .in3(RD31_24), .out(multiplexer_4_out), .sel(A[1:0]));
  Multiplexer #(.width(16), .enable("false")) multiplexer_5 (
    .in0({RD15_8, RD7_0}), .in1({RD31_24, RD23_16}), .out(multiplexer_5_out), .sel(A[1]));
  assign bit_extender_1_out = {{24{multiplexer_4_out[7]}}, multiplexer_4_out};  // Bit_Extender bit_extender_1
  assign bit_extender_2_out = {{16{multiplexer_5_out[15]}}, multiplexer_5_out};  // Bit_Extender bit_extender_2
  Multiplexer #(.select(2), .width(32), .enable("false")) multiplexer_6 (
    .in0({RD31_24, RD23_16, RD15_8, RD7_0}), .in1(bit_extender_2_out), .in2(bit_extender_1_out), .out(RD),
    .sel(DMop));  // open: in3

  // Other names for the same wires on the sheet: WD7_0[7:0] = WD[7:0]; WD15_8[7:0] = WD[15:8];
  //   RD_t[31:0] = {RD31_24, RD23_16, RD15_8, RD7_0}; op[1:0] = DMop; WD23_16[7:0] = WD[23:16];
  //   WD31_24[7:0] = WD[31:24]

  // Notes on the sheet:
  //   half word
  //   byte
endmodule

module Controller (
  input  [5:0] op,
  input  [5:0] funct,
  input  [1:0] comp,
  input  in_4,
  output [1:0] RegDst,
  output [2:0] ALUop,
  output ALUSrc,
  output [1:0] MemToReg,
  output RegWrite,
  output MemWrite,
  output [1:0] PCsel,
  output Extop,
  output [1:0] DMop
);

  wire add, and_1_out, and_2_out, beq, bitfinder_1_found, bitfinder_2_found, bitfinder_3_found,
       bitfinder_4_found, bitfinder_5_found, bomez, comparator_1_eq, comparator_2_eq, j, jal, jr, lb, lh,
       lui, lw, ori, sb, sh, sub, sw;
  wire [1:0] bitfinder_1_index, bitfinder_2_index, bitfinder_3_index, bitfinder_4_index, bitfinder_5_index,
       or_4_out, or_10_out;
  wire [2:0] bit_extender_1_out, or_7_out;
  wire [2:1] or_16_out;
  wire [3:0] or_12_out;

  Comparator #(.width(6), .mode("unsigned")) comparator_1 (
    .a(op), .b({6{1'b0}}), .eq(comparator_1_eq));  // open: gt, lt
  and u_add (add, comparator_1_eq, funct[5], ~funct[4], ~funct[3], ~funct[2], ~funct[1], ~funct[0]);  // AND_Gate
  and u_sub (sub, comparator_1_eq, funct[5], ~funct[4], ~funct[3], ~funct[2], funct[1], ~funct[0]);  // AND_Gate
  and u_ori (ori, ~comparator_1_eq, ~op[5], ~op[4], op[3], op[2], ~op[1], op[0]);  // AND_Gate
  and u_lw (lw, ~comparator_1_eq, op[5], ~op[4], ~op[3], ~op[2], op[1], op[0]);  // AND_Gate
  and u_sw (sw, ~comparator_1_eq, op[5], ~op[4], op[3], ~op[2], op[1], op[0]);  // AND_Gate
  and u_beq (beq, ~comparator_1_eq, ~op[5], ~op[4], ~op[3], op[2], ~op[1], ~op[0]);  // AND_Gate
  and u_lui (lui, ~comparator_1_eq, ~op[5], ~op[4], op[3], op[2], op[1], op[0]);  // AND_Gate
  and u_j (j, ~comparator_1_eq, ~op[5], ~op[4], ~op[3], ~op[2], op[1], ~op[0]);  // AND_Gate
  and u_jal (jal, ~comparator_1_eq, ~op[5], ~op[4], ~op[3], ~op[2], op[1], op[0]);  // AND_Gate
  and u_jr (jr, comparator_1_eq, ~funct[5], ~funct[4], funct[3], ~funct[2], ~funct[1], ~funct[0]);  // AND_Gate
  and u_lb (lb, ~comparator_1_eq, op[5], ~op[4], ~op[3], ~op[2], ~op[1], ~op[0]);  // AND_Gate
  and u_sb (sb, ~comparator_1_eq, op[5], ~op[4], op[3], ~op[2], ~op[1], ~op[0]);  // AND_Gate
  and u_lh (lh, ~comparator_1_eq, op[5], ~op[4], ~op[3], ~op[2], ~op[1], op[0]);  // AND_Gate
  and u_sh (sh, ~comparator_1_eq, op[5], ~op[4], op[3], ~op[2], ~op[1], op[0]);  // AND_Gate
  and u_bomez (bomez, ~comparator_1_eq, op[5], ~op[4], op[3], op[2], ~op[1], ~op[0]);  // AND_Gate
  or or_1 (or_12_out[1], sub, beq);
  buf or_2 (or_12_out[2], ori);  // OR_Gate
  buf or_3 (or_12_out[3], lui);  // OR_Gate
  or or_4 (or_4_out[0], add, sub, ori, lui);
  or or_5 (or_4_out[1], lw, lh, lb);
  or or_6 (MemWrite, sw, sh, sb);
  or or_7 (or_7_out[0], lw, sw);
  or or_8 (or_7_out[1], lh, sh);
  or or_9 (or_7_out[2], lb, sb);
  or or_10 (or_10_out[0], ori, lw, lui, lb);
  or or_11 (or_10_out[1], add, sub);
  or or_12 (or_12_out[0], lw, add, sw);
  or or_13 (ALUSrc, lh, ori, lw, sw, lui, lb, sb, sh);
  or or_14 (RegWrite, lh, add, sub, ori, lui, jal, lb, lw);
  and and_1 (and_1_out, beq, comparator_2_eq);
  Comparator #(.width(2)) comparator_2 (.a(comp), .b(2'b01), .eq(comparator_2_eq));  // open: gt, lt
  and and_2 (and_2_out, bomez, in_4);
  or or_15 (Extop, lw, sw, lb, sb, lh, sh);
  BitFinder #(.width(3)) bitfinder_1 (.in({jal, or_10_out}), .index(bitfinder_1_index), .found(bitfinder_1_found));
  BitFinder #(.width(3)) bitfinder_2 (.in({jal, or_4_out}), .index(bitfinder_2_index), .found(bitfinder_2_found));
  or or_16 (or_16_out[1], and_1_out, and_2_out);
  BitFinder #(.width(4)) bitfinder_3 (.in({1'b0, or_7_out}), .index(bitfinder_3_index), .found(bitfinder_3_found));
  Multiplexer #(.width(2), .enable("false")) multiplexer_1 (
    .in0(2'b00), .in1(bitfinder_1_index), .out(RegDst), .sel(bitfinder_1_found));
  BitFinder #(.width(4)) bitfinder_4 (.in(or_12_out), .index(bitfinder_4_index), .found(bitfinder_4_found));
  assign bit_extender_1_out = {{1{1'b0}}, bitfinder_4_index};  // Bit_Extender bit_extender_1
  Multiplexer #(.width(2), .enable("false")) multiplexer_2 (
    .in0(2'b00), .in1(bitfinder_2_index), .out(MemToReg), .sel(bitfinder_2_found));
  or or_17 (or_16_out[2], j, jal);
  Multiplexer #(.width(3), .enable("false")) multiplexer_3 (
    .in0(3'b000), .in1(bit_extender_1_out), .out(ALUop), .sel(bitfinder_4_found));
  Multiplexer #(.width(2), .enable("false")) multiplexer_4 (
    .in0(2'b00), .in1(bitfinder_3_index), .out(DMop), .sel(bitfinder_3_found));
  BitFinder #(.width(4), .\type ("high1")) bitfinder_5 (
    .in({jr, or_16_out, 1'b1}), .index(bitfinder_5_index), .found(bitfinder_5_found));
  Multiplexer #(.width(2), .enable("false")) multiplexer_5 (
    .in0(2'b00), .in1(bitfinder_5_index), .out(PCsel), .sel(bitfinder_5_found));
endmodule
