// Logisim project P0_L1_EXT.circ as structural Verilog: 1 circuit, main circuit ext
module ext (
  input  [15:0] in_1,
  input  [1:0] in_2,
  output [31:0] out_3
);

  // Probe on {{16{1'b0}}, in_1}
  // Probe on {in_1, {16{1'b0}}}
  // Probe on {{17{in_1[15]}}, in_1[14:0]}
  Multiplexer #(.select(2), .width(32), .enable("false")) multiplexer_1 (
    .in0({{16{1'b0}}, in_1}), .in1({{17{in_1[15]}}, in_1[14:0]}), .in2({in_1, {16{1'b0}}}),
    .in3({in_1[7:0], in_1[15:8], {16{in_1[15]}}}), .out(out_3), .sel(in_2));

  // Other names for the same wires on the sheet: datain[15:0] = in_1
endmodule
